// Logisim project Technik_5.circ as structural Verilog: 1 circuit, main circuit main
module main (
  input  M,
  input  s_l,
  input  s_r,
  output m_r_simple,
  output m_r_complex,
  output m_l_complex,
  output m_l_simple
);

  wire and_1_out, and_2_out, and_3_out, and_4_out, and_5_out, and_6_out, and_7_out, and_8_out, not_1_out,
       not_2_out, not_3_out;

  not not_1 (not_1_out, M);
  not not_2 (not_2_out, s_l);
  not not_3 (not_3_out, s_r);
  xor xor_1 (m_r_simple, M, s_l);
  and and_1 (and_1_out, not_1_out, s_l, not_3_out);
  and and_2 (and_2_out, not_1_out, s_l, s_r);
  and and_3 (and_3_out, M, not_2_out, not_3_out);
  and and_4 (and_4_out, M, not_2_out, s_r);
  and and_5 (and_5_out, not_1_out, not_2_out, s_r);
  and and_6 (and_6_out, not_1_out, s_l, s_r);
  and and_7 (and_7_out, M, not_2_out, not_3_out);
  and and_8 (and_8_out, M, s_l, not_3_out);
  or or_1 (m_r_complex, and_1_out, and_2_out, and_3_out, and_4_out);
  xor xor_2 (m_l_simple, M, s_r);
  or or_2 (m_l_complex, and_5_out, and_6_out, and_7_out, and_8_out);
endmodule
